// Logisim project Cond.circ as structural Verilog: 1 circuit, main circuit Cond
module Cond (
  input  [2:0] CC,
  input  [3:0] ifun,
  output Cnd
);

  wire G, GE, L, LE, NE;

  xor xor_1 (L, CC[1], CC[0]);
  not not_1 (GE, L);
  or or_1 (LE, L, CC[2]);
  not not_2 (G, LE);
  not not_3 (NE, CC[2]);
  Multiplexer #(.select(4), .enable("false")) multiplexer_1 (
    .in0(1'b1), .in1(LE), .in2(L), .in3(CC[2]), .in4(NE), .in5(GE), .in6(G), .in7(1'b0), .in8(1'b0),
    .in9(1'b0), .in10(1'b0), .in11(1'b0), .in12(1'b0), .in13(1'b0), .in14(1'b0), .in15(1'b0), .out(Cnd),
    .sel(ifun));

  // Other names for the same wires on the sheet: E = CC[2]

  // Notes on the sheet:
  //   OF
  //   SF
  //   ZF
endmodule
