// Logisim project NR_NC.circ as structural Verilog: 1 circuit, main circuit main
// SPLIT
module main (
  input  [7:0] Byte_0,
  input  imemerr,
  output [3:0] icode,
  output [3:0] ifun,
  output NR,
  output NC,
  output Inst__val
);

  wire and_1_out, and_2_out, and_3_out, and_4_out, and_5_out, and_6_out, multiplexer_1_out, not_1_out,
       not_2_out, not_3_out, not_4_out, not_5_out, not_6_out, not_7_out;

  not not_1 (not_1_out, Byte_0[6]);
  not not_2 (not_2_out, Byte_0[5]);
  not not_3 (not_3_out, Byte_0[4]);
  not not_4 (not_4_out, Byte_0[7]);
  not not_5 (not_5_out, Byte_0[5]);
  not not_6 (not_6_out, Byte_0[5]);
  not not_7 (not_7_out, Byte_0[4]);
  Multiplexer #(.select(4), .enable("false")) multiplexer_1 (
    .in0(1'b1), .in1(1'b1), .in2(1'b1), .in3(1'b1), .in4(1'b1), .in5(1'b1), .in6(1'b1), .in7(1'b1),
    .in8(1'b1), .in9(1'b1), .in10(1'b1), .in11(1'b1), .in12(1'b0), .in13(1'b0), .in14(1'b0), .in15(1'b0),
    .out(multiplexer_1_out), .sel(Byte_0[7:4]));
  and and_1 (and_1_out, not_1_out, Byte_0[5]);
  or or_1 (NR, and_1_out, and_2_out, and_3_out);
  and and_2 (and_2_out, Byte_0[6], not_2_out);
  and and_3 (and_3_out, Byte_0[6], not_3_out);
  and and_4 (and_4_out, not_4_out, Byte_0[5], Byte_0[4]);
  or or_2 (NC, and_4_out, and_5_out, and_6_out);
  and and_5 (and_5_out, Byte_0[6], not_5_out);
  and and_6 (and_6_out, Byte_0[7], not_6_out, not_7_out);
  and and_7 (Inst__val, ~imemerr, multiplexer_1_out);  // AND_Gate

  assign icode = Byte_0[7:4];
  assign ifun = Byte_0[3:0];

  // Other names for the same wires on the sheet: code[3:0] = Byte_0[7:4]
endmodule
