// Logisim project NewPC_32.circ as structural Verilog: 1 circuit, main circuit NewPC
// N_PC
module NewPC (
  input  cnd,
  input  [3:0] icode,
  input  [31:0] valC_0,
  input  [31:0] valP_0,
  input  [31:0] valM_0,
  output [31:0] val
);

  wire [31:0] multiplexer_1_out;

  Multiplexer #(.width(32), .enable("false")) multiplexer_1 (
    .in0(valP_0), .in1(valC_0), .out(multiplexer_1_out), .sel(cnd));
  Multiplexer #(.select(4), .width(32), .enable("false")) multiplexer_2 (
    .in0(valP_0), .in1(valP_0), .in2(valP_0), .in3(valP_0), .in4(valP_0), .in5(valP_0), .in6(valP_0),
    .in7(multiplexer_1_out), .in8(valC_0), .in9(valM_0), .in10(valP_0), .in11(valP_0), .in12(valP_0),
    .in13(valP_0), .in14(valP_0), .in15(valP_0), .out(val), .sel(icode));

  // Other names for the same wires on the sheet: cndT = cnd
endmodule
