// Logisim project PC_incrementer.circ as structural Verilog: 1 circuit, main circuit main
// PC++
module main (
  input  NR,
  input  NC,
  input  [31:0] current_PC,
  output [31:0] ValP
);

  wire [3:0] multiplexer_1_out;
  wire [31:0] bit_extender_1_out;

  Multiplexer #(.select(2), .width(4), .disabled(0)) multiplexer_1 (
    .in0(4'b0001), .in1(4'b0010), .in2(4'b1001), .in3(4'b1010), .out(multiplexer_1_out), .sel({NC, NR}),
    .en(1'b1));
  assign bit_extender_1_out = {{28{1'b0}}, multiplexer_1_out};  // Bit_Extender bit_extender_1
  Adder #(.width(32)) adder_1 (.a(bit_extender_1_out), .b(current_PC), .out(ValP));  // open: cin, cout
endmodule
