// Logisim project Prep_ALU.circ as structural Verilog: 5 circuits, main circuit main
// Prep ALU
module main (
  input  [3:0] icode,
  input  [3:0] ifun,
  input  [31:0] valA_1,
  input  [31:0] valA_0,
  input  [31:0] ValB_1,
  input  [31:0] ValB_0,
  input  [31:0] valC_1,
  input  [31:0] valC_0,
  output need_CC,
  output [31:0] aluA_1,
  output [31:0] aluA_0,
  output [31:0] aluB_1,
  output [31:0] aluB_0,
  output [3:0] alu_fun
);

  Set_CC set_cc_1 (.icode(icode), .needCC(need_CC));
  ALU_A alu_a_1 (
    .valA_1(valA_1), .valA_0(valA_0), .valC_1(valC_1), .valC_0(valC_0), .icode(icode), .valA_1_2(aluA_1),
    .valA_0_2(aluA_0));
  ALU_B alu_b_1 (.valB_1(ValB_1), .valB_0(ValB_0), .icode(icode), .valB_1_2(aluB_1), .valB_0_2(aluB_0));
  ALU_FUN alu_fun_1 (.ifun(ifun), .icode(icode), .alu_f_out(alu_fun));

  // Other names for the same wires on the sheet: fun[3:0] = ifun
endmodule

// A
module ALU_A (
  input  [3:0] icode,
  input  [31:0] valA_1,
  input  [31:0] valA_0,
  input  [31:0] valC_1,
  input  [31:0] valC_0,
  output [31:0] valA_1_2,
  output [31:0] valA_0_2
);

  Multiplexer #(.select(4), .width(32)) multiplexer_1 (
    .in0({32{1'b0}}), .in1({32{1'b0}}), .in2(valA_1), .in3(valC_1), .in4(valC_1), .in5(valC_1), .in6(valA_1),
    .in7({32{1'b0}}), .in8({32{1'b1}}), .in9({32{1'b0}}), .in10({32{1'b1}}), .in11({32{1'b0}}),
    .in12({32{1'b0}}), .in13({32{1'b0}}), .in14({32{1'b0}}), .in15({32{1'b0}}), .out(valA_1_2), .sel(icode),
    .en(1'b1));
  Multiplexer #(.select(4), .width(32)) multiplexer_2 (
    .in0({32{1'b0}}), .in1({32{1'b0}}), .in2(valA_0), .in3(valC_0), .in4(valC_0), .in5(valC_0), .in6(valA_0),
    .in7({32{1'b0}}), .in8(32'hfffffff8), .in9(32'h8), .in10(32'hfffffff8), .in11(32'h8), .in12({32{1'b0}}),
    .in13({32{1'b0}}), .in14({32{1'b0}}), .in15({32{1'b0}}), .out(valA_0_2), .sel(icode), .en(1'b1));
endmodule

// B
module ALU_B (
  input  [3:0] icode,
  input  [31:0] valB_1,
  input  [31:0] valB_0,
  output [31:0] valB_1_2,
  output [31:0] valB_0_2
);

  Multiplexer #(.select(4), .width(32)) multiplexer_1 (
    .in0({32{1'b0}}), .in1({32{1'b0}}), .in2({32{1'b0}}), .in3({32{1'b0}}), .in4(valB_1), .in5(valB_1),
    .in6(valB_1), .in7({32{1'b0}}), .in8(valB_1), .in9(valB_1), .in10(valB_1), .in11(valB_1),
    .in12({32{1'b0}}), .in13({32{1'b0}}), .in14({32{1'b0}}), .in15({32{1'b0}}), .out(valB_1_2), .sel(icode),
    .en(1'b1));
  Multiplexer #(.select(4), .width(32)) multiplexer_2 (
    .in0({32{1'b0}}), .in1({32{1'b0}}), .in2({32{1'b0}}), .in3({32{1'b0}}), .in4(valB_0), .in5(valB_0),
    .in6(valB_0), .in7({32{1'b0}}), .in8(valB_0), .in9(valB_0), .in10(valB_0), .in11(valB_0),
    .in12({32{1'b0}}), .in13({32{1'b0}}), .in14({32{1'b0}}), .in15({32{1'b0}}), .out(valB_0_2), .sel(icode),
    .en(1'b1));
endmodule

// FUN
module ALU_FUN (
  input  [3:0] icode,
  input  [3:0] ifun,
  output [3:0] alu_f_out
);

  wire and_1_out;
  wire [3:0] xnor_1_out;

  // Probe on xnor_1_out
  assign xnor_1_out = ~(icode ^ 4'b0110);  // XNOR_Gate xnor_1, 4 bits wide
  and and_1 (and_1_out, xnor_1_out[0], xnor_1_out[1], xnor_1_out[2], xnor_1_out[3]);
  Multiplexer #(.width(4), .enable("false")) multiplexer_1 (
    .in0(4'b0000), .in1(ifun), .out(alu_f_out), .sel(and_1_out));
endmodule

module Set_CC (
  input  [3:0] icode,
  output needCC
);

  wire not_1_out, not_2_out;

  not not_1 (not_1_out, icode[3]);
  not not_2 (not_2_out, icode[0]);
  and and_1 (needCC, not_1_out, icode[2], icode[1], not_2_out);
endmodule
