// Logisim project Prep_Mem.circ as structural Verilog: 4 circuits, main circuit Prep_Mem
// P_Mem
module Prep_Mem (
  input  [3:0] icode,
  input  [31:0] valE_1,
  input  [31:0] valE_0,
  input  [31:0] valA_1,
  input  [31:0] valA_0,
  input  [31:0] valP_1,
  input  [31:0] valP_0,
  output [31:0] addr_1,
  output [31:0] addr_0,
  output [31:0] data_1,
  output [31:0] data_0,
  output R,
  output W
);

  Mem__Addr mem_addr_1 (
    .valE_1(valE_1), .valE_0(valE_0), .valA_1(valA_1), .valA_0(valA_0), .icode(icode), .addr_1(addr_1),
    .addr_0(addr_0));
  Mem__Data DATA (
    .valP_1(valP_1), .valP_0(valP_0), .valA_1(valA_1), .valA_0(valA_0), .icode(icode), .data_1(data_1),
    .data_0(data_0));
  R_W R_W (.icode(icode), .R(R), .W(W));
endmodule

// ADDR
module Mem__Addr (
  input  [31:0] valE_1,
  input  [31:0] valE_0,
  input  [31:0] valA_1,
  input  [31:0] valA_0,
  input  [3:0] icode,
  output [31:0] addr_1,
  output [31:0] addr_0
);

  Multiplexer #(.select(4), .width(32), .enable("false")) multiplexer_1 (
    .in0({32{1'b0}}), .in1({32{1'b0}}), .in2({32{1'b0}}), .in3({32{1'b0}}), .in4(valE_1), .in5(valE_1),
    .in6({32{1'b0}}), .in7({32{1'b0}}), .in8(valE_1), .in9(valA_1), .in10(valE_1), .in11(valA_1),
    .in12({32{1'b0}}), .in13({32{1'b0}}), .in14({32{1'b0}}), .in15({32{1'b0}}), .out(addr_1), .sel(icode));
  Multiplexer #(.select(4), .width(32), .enable("false")) multiplexer_2 (
    .in0({32{1'b0}}), .in1({32{1'b0}}), .in2({32{1'b0}}), .in3({32{1'b0}}), .in4(valE_0), .in5(valE_0),
    .in6({32{1'b0}}), .in7({32{1'b0}}), .in8(valE_0), .in9(valA_0), .in10(valE_0), .in11(valA_0),
    .in12({32{1'b0}}), .in13({32{1'b0}}), .in14({32{1'b0}}), .in15({32{1'b0}}), .out(addr_0), .sel(icode));
endmodule

// DATA
module Mem__Data (
  input  [31:0] valP_1,
  input  [31:0] valP_0,
  input  [31:0] valA_1,
  input  [31:0] valA_0,
  input  [3:0] icode,
  output [31:0] data_1,
  output [31:0] data_0
);

  Multiplexer #(.select(4), .width(32), .enable("false")) multiplexer_1 (
    .in0({32{1'b0}}), .in1({32{1'b0}}), .in2({32{1'b0}}), .in3({32{1'b0}}), .in4(valA_1), .in5({32{1'b0}}),
    .in6({32{1'b0}}), .in7({32{1'b0}}), .in8(valP_1), .in9({32{1'b0}}), .in10(valA_1), .in11({32{1'b0}}),
    .in12({32{1'b0}}), .in13({32{1'b0}}), .in14({32{1'b0}}), .in15({32{1'b0}}), .out(data_1), .sel(icode));
  Multiplexer #(.select(4), .width(32), .enable("false")) multiplexer_2 (
    .in0({32{1'b0}}), .in1({32{1'b0}}), .in2({32{1'b0}}), .in3({32{1'b0}}), .in4(valA_0), .in5({32{1'b0}}),
    .in6({32{1'b0}}), .in7({32{1'b0}}), .in8(valP_0), .in9({32{1'b0}}), .in10(valA_0), .in11({32{1'b0}}),
    .in12({32{1'b0}}), .in13({32{1'b0}}), .in14({32{1'b0}}), .in15({32{1'b0}}), .out(data_0), .sel(icode));
endmodule

module R_W (
  input  [3:0] icode,
  output R,
  output W
);

  wire and_1_out, and_2_out, and_3_out, and_4_out, and_5_out, not_1_out, not_2_out, not_3_out, not_4_out;

  not not_1 (not_1_out, icode[1]);
  not not_2 (not_2_out, icode[1]);
  not not_3 (not_3_out, icode[0]);
  not not_4 (not_4_out, icode[0]);
  and and_1 (and_1_out, icode[2], not_1_out, icode[0]);
  and and_2 (and_2_out, icode[3], icode[0]);
  and and_3 (and_3_out, icode[2], not_2_out, not_3_out);
  and and_4 (and_4_out, icode[3], not_4_out);
  and and_5 (and_5_out, icode[3], icode[2]);
  or or_1 (R, and_1_out, and_2_out);
  or or_2 (W, and_3_out, and_4_out, and_5_out);
endmodule
