// Logisim project RegInput.circ as structural Verilog: 5 circuits, main circuit main
// A.B.E.M.
module main (
  input  [3:0] icode,
  input  Cnd,
  input  [3:0] rA,
  input  [3:0] rB,
  output [3:0] SrcA,
  output [3:0] SrcB,
  output [3:0] DstE,
  output [3:0] DstM
);

  SrcA srca_1 (.icode(icode), .rA(rA), .src_A(SrcA));
  SrcB srcb_1 (.icode(icode), .rB(rB), .src_B(SrcB));
  DstE dste_1 (.icode(icode), .rB(rB), .Cnd(Cnd), .dest_m(DstE));
  DstM dstm_1 (.icode(icode), .rA(rA), .dest_m(DstM));
endmodule

module SrcA (
  input  [3:0] icode,
  input  [3:0] rA,
  output [3:0] src_A
);

  wire and_1_out, and_2_out, needRA, needRSP, not_1_out, not_2_out, not_3_out, not_4_out, not_5_out;

  Multiplexer #(.select(2), .width(4)) multiplexer_1 (
    .in0(4'b1111), .in1(4'b0100), .in2(rA), .out(src_A), .sel({needRA, needRSP}), .en(1'b1));  // open: in3
  not not_1 (not_1_out, icode[2]);
  and and_1 (and_1_out, not_1_out, icode[1], not_2_out);
  not not_2 (not_2_out, icode[0]);
  not not_3 (not_3_out, icode[3]);
  and and_2 (and_2_out, not_3_out, icode[2], not_4_out);
  not not_4 (not_4_out, icode[0]);
  not not_5 (not_5_out, icode[2]);
  and and_3 (needRSP, icode[3], not_5_out, icode[0]);
  or or_1 (needRA, and_1_out, and_2_out);
endmodule

module SrcB (
  input  [3:0] icode,
  input  [3:0] rB,
  output [3:0] src_B
);

  wire and_1_out, and_2_out, needRB, needRSP, not_1_out, not_2_out, not_3_out, not_4_out, not_5_out;

  Multiplexer #(.select(2), .width(4)) multiplexer_1 (
    .in0(4'b1111), .in1(4'b0100), .in2(rB), .out(src_B), .sel({needRB, needRSP}), .en(1'b1));  // open: in3
  not not_1 (not_1_out, icode[3]);
  not not_2 (not_2_out, icode[1]);
  not not_3 (not_3_out, icode[3]);
  not not_4 (not_4_out, icode[0]);
  not not_5 (not_5_out, icode[2]);
  and and_1 (and_1_out, not_1_out, icode[2], not_2_out);
  and and_2 (and_2_out, not_3_out, icode[2], not_4_out);
  and and_3 (needRSP, icode[3], not_5_out);
  or or_1 (needRB, and_1_out, and_2_out);
endmodule

module DstE (
  input  [3:0] icode,
  input  [3:0] rB,
  input  Cnd,
  output [3:0] dest_m
);

  wire and_1_out, and_2_out, and_3_out, needRB, needRB_2, needRSP, not_1_out, not_2_out, not_3_out,
       not_4_out, not_5_out, not_6_out, not_7_out, not_8_out;
  wire [1:1] or_1_out;

  and and_1 (and_1_out, needRB_2, Cnd);
  or or_1 (or_1_out[1], needRB, and_1_out);
  Multiplexer #(.select(2), .width(4)) multiplexer_1 (
    .in0(4'b1111), .in1(4'b0100), .in2(rB), .out(dest_m), .sel({or_1_out[1], needRSP}), .en(1'b1));  // open: in3
  not not_1 (not_1_out, icode[3]);
  not not_2 (not_2_out, icode[2]);
  not not_3 (not_3_out, icode[3]);
  not not_4 (not_4_out, icode[0]);
  not not_5 (not_5_out, icode[3]);
  not not_6 (not_6_out, icode[2]);
  not not_7 (not_7_out, icode[0]);
  not not_8 (not_8_out, icode[2]);
  and and_2 (and_2_out, not_1_out, not_2_out, icode[1], icode[0]);
  and and_3 (and_3_out, not_3_out, icode[2], icode[1], not_4_out);
  and and_4 (needRB_2, not_5_out, not_6_out, icode[1], not_7_out);
  and and_5 (needRSP, icode[3], not_8_out);
  or or_2 (needRB, and_2_out, and_3_out);
endmodule

module DstM (
  input  [3:0] icode,
  input  [3:0] rA,
  output [3:0] dest_m
);

  wire and_1_out, and_2_out, needRA, not_1_out, not_2_out, not_3_out;

  not not_1 (not_1_out, icode[3]);
  not not_2 (not_2_out, icode[1]);
  not not_3 (not_3_out, icode[2]);
  Multiplexer #(.width(4)) multiplexer_1 (.in0(4'b1111), .in1(rA), .out(dest_m), .sel(needRA), .en(1'b1));
  and and_1 (and_1_out, not_1_out, icode[2], not_2_out, icode[0]);
  and and_2 (and_2_out, icode[3], not_3_out, icode[1], icode[0]);
  or or_1 (needRA, and_1_out, and_2_out);
endmodule
