// Logisim project alu.circ as structural Verilog: 3 circuits, main circuit aluSlice
// ALU
module alu (
  input  [31:0] aluA_1,
  input  [31:0] aluA_0,
  input  [31:0] aluB_1,
  input  [31:0] aluB_0,
  input  [3:0] ALUfun,
  output out_6,
  output out_7,
  output out_8,
  output [31:0] valE_1,
  output [31:0] valE_0
);

  wire aluslice_1_zf, aluslice_2_cout, aluslice_2_zf, and_1_out;
  wire [31:0] multiplexer_1_out, multiplexer_2_out, not_1_out, not_2_out;

  assign not_1_out = ~aluA_1;  // NOT_Gate not_1, 32 bits wide
  assign not_2_out = ~aluA_0;  // NOT_Gate not_2, 32 bits wide
  Multiplexer #(.width(32), .enable("false")) multiplexer_1 (
    .in0(aluA_1), .in1(not_1_out), .out(multiplexer_1_out), .sel(and_1_out));
  Multiplexer #(.width(32), .enable("false")) multiplexer_2 (
    .in0(aluA_0), .in1(not_2_out), .out(multiplexer_2_out), .sel(and_1_out));
  and and_1 (and_1_out, ~ALUfun[1], ALUfun[0]);  // AND_Gate
  and and_2 (out_6, aluslice_2_zf, aluslice_1_zf);
  aluSlice aluslice_1 (
    .ALU_A(multiplexer_1_out), .ALU_B(aluB_1), .valE(valE_1), .ZF(aluslice_1_zf), .SF(out_7), .OF(out_8),
    .ALUfun(ALUfun), .Cin(aluslice_2_cout));  // open: Cout
  aluSlice aluslice_2 (
    .ALU_A(multiplexer_2_out), .ALU_B(aluB_0), .valE(valE_0), .ZF(aluslice_2_zf), .ALUfun(ALUfun),
    .Cin(and_1_out), .Cout(aluslice_2_cout));  // open: SF, OF
endmodule

module aluSlice (
  input  Cin,
  input  [31:0] ALU_A,
  input  [31:0] ALU_B,
  input  [3:0] ALUfun,
  output ZF,
  output SF,
  output OF,
  output Cout,
  output [31:0] valE
);

  wire msb32_1_msb, msb32_2_msb, or_1_out, xnor_1_out, xor_1_out;
  wire [5:0] bitadder_1_out;
  wire [31:0] adder_1_out, and_2_out, multiplexer_1_out, xor_2_out;

  xnor xnor_1 (xnor_1_out, msb32_1_msb, msb32_2_msb);
  msb32 msb32_1 (.msb(msb32_1_msb), .val(ALU_A));
  msb32 msb32_2 (.msb(msb32_2_msb), .val(ALU_B));
  and and_1 (OF, xnor_1_out, xor_1_out);
  Adder #(.width(32)) adder_1 (.a(ALU_B), .b(ALU_A), .out(adder_1_out), .cin(Cin), .cout(Cout));
  xor xor_1 (xor_1_out, msb32_2_msb, SF);
  msb32 msb32_3 (.msb(SF), .val(adder_1_out));
  assign and_2_out = ALU_A & ALU_B;  // AND_Gate and_2, 32 bits wide
  assign xor_2_out = ALU_A ^ ALU_B;  // XOR_Gate xor_2, 32 bits wide
  Multiplexer #(.width(32), .enable("false")) multiplexer_1 (
    .in0(and_2_out), .in1(xor_2_out), .out(multiplexer_1_out), .sel(ALUfun[0]));
  not not_1 (ZF, or_1_out);
  Multiplexer #(.width(32), .enable("false")) multiplexer_2 (
    .in0(adder_1_out), .in1(multiplexer_1_out), .out(valE), .sel(ALUfun[1]));
  or or_1 (or_1_out, bitadder_1_out[5], bitadder_1_out[4], bitadder_1_out[3], bitadder_1_out[2], bitadder_1_out[1], bitadder_1_out[0]);
  BitAdder #(.width(32)) bitadder_1 (.in0(valE), .out(bitadder_1_out));
endmodule

module msb32 (
  input  [31:0] val,
  output msb
);


  assign msb = val[31];
endmodule
