// Logisim project dmem_EXAM.circ as structural Verilog: 1 circuit, main circuit dmem
module dmem (
  input  [31:0] Addr_1,
  input  [31:0] Addr_0,
  input  [31:0] Data_1,
  input  [31:0] Data_0,
  input  read,
  input  write,
  input  clock,
  input  dataclear,
  output [31:0] valM_1,
  output [31:0] valM_0,
  output dmemerr
);

  wire bitfinder_1_found, bitfinder_2_found, or_1_out, or_2_out;
  wire [6:0] adder_1_out, multiplexer_1_out, multiplexer_2_out;
  wire [31:0] ram_1_data, ram_2_data;

  BitFinder #(.width(32)) bitfinder_1 (.in(Addr_1), .found(bitfinder_1_found));  // open: index
  BitFinder #(.width(22)) bitfinder_2 (.in(Addr_0[31:10]), .found(bitfinder_2_found));  // open: index
  or or_1 (or_1_out, bitfinder_1_found, bitfinder_2_found, Addr_0[1], Addr_0[0]);
  Adder #(.width(7)) adder_1 (.a({7{1'b0}}), .b(Addr_0[9:3]), .out(adder_1_out));  // open: cin, cout
  or or_2 (or_2_out, read, write);
  and and_1 (dmemerr, or_1_out, or_2_out);
  Multiplexer #(.width(7), .enable("false")) multiplexer_1 (
    .in0({7{1'b0}}), .in1(adder_1_out), .out(multiplexer_1_out), .sel(or_2_out));
  Multiplexer #(.width(7), .enable("false")) multiplexer_2 (
    .in0({7{1'b0}}), .in1(Addr_0[9:3]), .out(multiplexer_2_out), .sel(or_2_out));
  RAM #(.addrWidth(7), .dataWidth(32), .bus("separate")) ram_1 (
    .addr(multiplexer_1_out), .din(Data_0), .data(ram_1_data), .str(write), .clk(clock), .ld(or_2_out),
    .clr(dataclear));  // open: sel
  RAM #(.addrWidth(7), .dataWidth(32), .bus("separate")) ram_2 (
    .addr(multiplexer_2_out), .din(Data_1), .data(ram_2_data), .str(write), .clk(clock), .ld(or_2_out),
    .clr(dataclear));  // open: sel
  Multiplexer #(.width(32), .enable("false")) multiplexer_3 (
    .in0(ram_1_data), .in1(ram_2_data), .out(valM_0), .sel(Addr_0[2]));
  Multiplexer #(.width(32), .enable("false")) multiplexer_4 (
    .in0(ram_2_data), .in1(ram_1_data), .out(valM_1), .sel(Addr_0[2]));
endmodule
