// Logisim project imem_EXAM.circ as structural Verilog: 4 circuits, main circuit imem
module imem (
  input  [31:0] in_1,
  output [7:0] out_2,
  output [7:0] out_3,
  output [7:0] out_4,
  output [7:0] out_5,
  output [7:0] out_6,
  output [7:0] out_7,
  output [7:0] out_8,
  output [7:0] out_9,
  output [7:0] out_10,
  output imemerr,
  output [7:0] out_12
);

  wire bankaddr_1_error, bankaddr_2_error, bankaddr_3_error, bankaddr_4_error;
  wire [3:0] low4_1_out_2;
  wire [7:0] bankaddr_1_bankaddr, bankaddr_2_bankaddr, bankaddr_3_bankaddr, bankaddr_4_bankaddr;
  wire [31:0] rom_1_data, rom_2_data, rom_3_data, rom_4_data;

  Low4 low4_1 (.in_1(in_1), .out_2(low4_1_out_2));
  BankAddr bankaddr_1 (.BankIndex(2'b00), .FullAddr(in_1), .BankAddr(bankaddr_1_bankaddr), .Error(bankaddr_1_error));
  BankAddr bankaddr_2 (.BankIndex(2'b01), .FullAddr(in_1), .BankAddr(bankaddr_2_bankaddr), .Error(bankaddr_2_error));
  BankAddr bankaddr_3 (.BankIndex(2'b10), .FullAddr(in_1), .BankAddr(bankaddr_3_bankaddr), .Error(bankaddr_3_error));
  BankAddr bankaddr_4 (.BankIndex(2'b11), .FullAddr(in_1), .BankAddr(bankaddr_4_bankaddr), .Error(bankaddr_4_error));
  or or_1 (imemerr, bankaddr_1_error, bankaddr_2_error, bankaddr_3_error, bankaddr_4_error);
  ROM #(.dataWidth(32)) rom_1 (.addr(bankaddr_1_bankaddr), .data(rom_1_data));  // open: sel
  ROM #(.dataWidth(32)) rom_2 (.addr(bankaddr_2_bankaddr), .data(rom_2_data));  // open: sel
  ROM #(.dataWidth(32)) rom_3 (.addr(bankaddr_3_bankaddr), .data(rom_3_data));  // open: sel
  ROM #(.dataWidth(32)) rom_4 (.addr(bankaddr_4_bankaddr), .data(rom_4_data));  // open: sel
  BankMux4 bankmux4_1 (
    .Bank0(rom_1_data), .Bank1(rom_2_data), .Bank2(rom_3_data), .Bank3(rom_4_data), .AddrLow(low4_1_out_2),
    .Index(4'b0000), .OutByte(out_2));
  BankMux4 bankmux4_2 (
    .Bank0(rom_1_data), .Bank1(rom_2_data), .Bank2(rom_3_data), .Bank3(rom_4_data), .AddrLow(low4_1_out_2),
    .Index(4'b0001), .OutByte(out_3));
  BankMux4 bankmux4_3 (
    .Bank0(rom_1_data), .Bank1(rom_2_data), .Bank2(rom_3_data), .Bank3(rom_4_data), .AddrLow(low4_1_out_2),
    .Index(4'b0010), .OutByte(out_4));
  BankMux4 bankmux4_4 (
    .Bank0(rom_1_data), .Bank1(rom_2_data), .Bank2(rom_3_data), .Bank3(rom_4_data), .AddrLow(low4_1_out_2),
    .Index(4'b0011), .OutByte(out_5));
  BankMux4 bankmux4_5 (
    .Bank0(rom_1_data), .Bank1(rom_2_data), .Bank2(rom_3_data), .Bank3(rom_4_data), .AddrLow(low4_1_out_2),
    .Index(4'b0100), .OutByte(out_6));
  BankMux4 bankmux4_6 (
    .Bank0(rom_1_data), .Bank1(rom_2_data), .Bank2(rom_3_data), .Bank3(rom_4_data), .AddrLow(low4_1_out_2),
    .Index(4'b0101), .OutByte(out_7));
  BankMux4 bankmux4_7 (
    .Bank0(rom_1_data), .Bank1(rom_2_data), .Bank2(rom_3_data), .Bank3(rom_4_data), .AddrLow(low4_1_out_2),
    .Index(4'b0110), .OutByte(out_8));
  BankMux4 bankmux4_8 (
    .Bank0(rom_1_data), .Bank1(rom_2_data), .Bank2(rom_3_data), .Bank3(rom_4_data), .AddrLow(low4_1_out_2),
    .Index(4'b0111), .OutByte(out_9));
  BankMux4 bankmux4_9 (
    .Bank0(rom_1_data), .Bank1(rom_2_data), .Bank2(rom_3_data), .Bank3(rom_4_data), .AddrLow(low4_1_out_2),
    .Index(4'b1000), .OutByte(out_10));
  BankMux4 bankmux4_10 (
    .Bank0(rom_1_data), .Bank1(rom_2_data), .Bank2(rom_3_data), .Bank3(rom_4_data), .AddrLow(low4_1_out_2),
    .Index(4'b1001), .OutByte(out_12));

  // Notes on the sheet:
  //   contents of rom_1 (hex, n*v repeats v):
  //   30f40002 0 3000000 30f71800 0 6266718c 0 ff60a630 4e000000
  //   contents of rom_2 (hex, n*v repeats v):
  //   4*0 804e0000 0 30 fa080000
  //   contents of rom_3 (hex, n*v repeats v):
  //   8030 5000000 7000000 30f6 0 a0 faffffff 0 6030b03f
  //   contents of rom_4 (hex, n*v repeats v):
  //   0 0 0 3000000 906300 3f503700 ffffffff 60a780 90000000
endmodule

module Low4 (
  input  [31:0] in_1,
  output [3:0] out_2
);


  assign out_2 = in_1[3:0];
endmodule

module BankAddr (
  input  [1:0] BankIndex,
  input  [31:0] FullAddr,
  output [7:0] BankAddr,
  output Error
);

  wire subtractor_1_bout;

  // Probe on FullAddr
  // Probe on FullAddr[3:2]
  Subtractor #(.width(2)) subtractor_1 (.a(BankIndex), .b(FullAddr[3:2]), .bout(subtractor_1_bout));  // open: out, bin
  Adder adder_1 (.a({8{1'b0}}), .b(FullAddr[11:4]), .out(BankAddr), .cin(subtractor_1_bout));  // open: cout
  or or_1 (Error, FullAddr[12], FullAddr[13], FullAddr[14], FullAddr[15], FullAddr[16], FullAddr[17], FullAddr[18], FullAddr[19], FullAddr[20], FullAddr[21], FullAddr[22], FullAddr[23], FullAddr[24], FullAddr[25], FullAddr[26], FullAddr[27], FullAddr[28], FullAddr[29], FullAddr[30], FullAddr[31]);
endmodule

module BankMux4 (
  input  [31:0] Bank0,
  input  [31:0] Bank1,
  input  [31:0] Bank2,
  input  [31:0] Bank3,
  input  [3:0] AddrLow,
  input  [3:0] Index,
  output [7:0] OutByte
);

  wire [3:0] adder_1_out;

  Adder #(.width(4)) adder_1 (.a(AddrLow), .b(Index), .out(adder_1_out));  // open: cin, cout
  Multiplexer #(.select(4), .width(8), .enable("false")) multiplexer_1 (
    .in0(Bank0[31:24]), .in1(Bank0[23:16]), .in2(Bank0[15:8]), .in3(Bank0[7:0]), .in4(Bank1[31:24]),
    .in5(Bank1[23:16]), .in6(Bank1[15:8]), .in7(Bank1[7:0]), .in8(Bank2[31:24]), .in9(Bank2[23:16]),
    .in10(Bank2[15:8]), .in11(Bank2[7:0]), .in12(Bank3[31:24]), .in13(Bank3[23:16]), .in14(Bank3[15:8]),
    .in15(Bank3[7:0]), .out(OutByte), .sel(adder_1_out));
endmodule
