// Logisim project stat.circ as structural Verilog: 1 circuit, main circuit main
// stat
module main (
  input  [3:0] icode,
  input  insrval,
  input  imemerr,
  input  dmemerr,
  output [1:0] out_5
);

  wire and_1_out, and_2_out, and_3_out, not_1_out, not_2_out, not_3_out, or_1_out;

  not not_1 (not_1_out, insrval);
  and and_1 (and_1_out, ~icode[0], ~icode[1], ~icode[2], ~icode[3]);  // AND_Gate
  not not_2 (not_2_out, not_1_out);
  not not_3 (not_3_out, not_1_out);
  and and_2 (and_2_out, not_2_out, dmemerr);
  or or_1 (or_1_out, and_2_out, and_3_out);
  and and_3 (and_3_out, not_3_out, imemerr);
  or or_2 (out_5[1], and_1_out, not_1_out);
  or or_3 (out_5[0], and_1_out, or_1_out);
endmodule
