// Logisim project y86.circ as structural Verilog
module main (
  input  Reset
);

  wire and_1_out, Clock_out, Cnd, dmemerr, imemerr, Ins_V, main_5_need_cc, Need_Reg, Need_ValC, nor_1_out,
       not_1_out, prep_mem_1_r, prep_mem_1_w;
  wire [1:0] main_2_out_5, Stat_q;
  wire [2:0] alu_1_out_8, register_1_q;
  wire [3:0] align_1_ra, align_1_rb, destE, destM, icode, ifun, main_5_alu_fun, srcA, srcB;
  wire [7:0] imem_1_p3, imem_1_p4, imem_1_p5, imem_1_p6, imem_1_p7, imem_1_p8, imem_1_p9, imem_1_p10,
       imem_1_p11, imem_1_p12;
  wire [31:0] Addr_0, Addr_1, aluA_0, aluA_1, aluB_0, aluB_1, Data_0, Data_1, N_PC_output, NewPC, PC_q,
       valA_0, valA_1, valB_0, valB_1, valC_0, valC_1, valE_0, valE_1, valM_0, valM_1, valP;

  and and_1 (and_1_out, Clock_out, nor_1_out);
  Clock Clock (.out(Clock_out));
  Register #(.width(32)) PC (.D(NewPC), .Q(PC_q), .clk(and_1_out), .clr(Reset));  // open: en
  nor nor_1 (nor_1_out, Stat_q[1], Stat_q[0]);
  // Probe on valP
  PC_incrementer_main main_1 (.current_PC(PC_q), .NR(Need_Reg), .NC(Need_ValC), .ValP(valP));
  not not_1 (not_1_out, and_1_out);
  stat_main main_2 (.insrval(Ins_V), .imemerr(imemerr), .dmemerr(dmemerr), .icode(icode), .out_5(main_2_out_5));
  // Probe on main_2_out_5
  // Probe on icode
  // Probe on icode
  // Probe on ifun
  // Probe on ifun
  NR_NC_main main_3 (
    .Byte_0(imem_1_p3), .imemerr(imemerr), .icode(icode), .ifun(ifun), .NR(Need_Reg), .NC(Need_ValC),
    .Inst__val(Ins_V));
  // imem imem_1: pin names not known; wires that end beside it: PC_q, imemerr, imem_1_p3, imem_1_p4, imem_1_p5, imem_1_p6, imem_1_p7, imem_1_p8, imem_1_p9, imem_1_p10, imem_1_p11, imem_1_p12
  Align align_1 (
    .B1(imem_1_p4), .B2(imem_1_p5), .B3(imem_1_p6), .B4(imem_1_p7), .B5(imem_1_p8), .B6(imem_1_p9),
    .B7(imem_1_p10), .B8(imem_1_p11), .B9(imem_1_p12), .NeedRegs(Need_Reg), .rA(align_1_ra), .rB(align_1_rb),
    .valC_1(valC_1), .valC_0(valC_0));
  Register #(.width(2)) Stat (.D(main_2_out_5), .Q(Stat_q), .clk(not_1_out), .clr(Reset));  // open: en
  // Probe on valC_1
  // Probe on valC_0
  RegInput_main main_4 (
    .rA(align_1_ra), .rB(align_1_rb), .icode(icode), .Cnd(Cnd), .SrcA(srcA), .SrcB(srcB), .DstE(destE),
    .DstM(destM));
  // Probe on srcA
  // Probe on srcB
  // Probe on valA_1
  // Probe on valA_0
  regfile regfile_1 (
    .srcA(srcA), .srcB(srcB), .dstE(destE), .valE_1(valE_1), .valE_0(valE_0), .dstM(destM), .valM_1(valM_1),
    .valM_0(valM_0), .valA_1(valA_1), .valA_0(valA_0), .valB_1(valB_1), .valB_0(valB_0), .in_9(not_1_out),
    .in_10(Reset));
  // Probe on destE
  // Probe on destM
  Prep_ALU_main main_5 (
    .valA_1(valA_1), .valA_0(valA_0), .ValB_1(valB_1), .ValB_0(valB_0), .valC_1(valC_1), .valC_0(valC_0),
    .icode(icode), .ifun(ifun), .need_CC(main_5_need_cc), .aluA_1(aluA_1), .aluA_0(aluA_0), .aluB_1(aluB_1),
    .aluB_0(aluB_0), .alu_fun(main_5_alu_fun));
  // Probe on valB_1
  // Probe on valB_0
  alu alu_1 (
    .aluA_1(aluA_1), .aluA_0(aluA_0), .aluB_1(aluB_1), .aluB_0(aluB_0), .out_6(alu_1_out_8[2]),
    .out_7(alu_1_out_8[1]), .out_8(alu_1_out_8[0]), .ALUfun(main_5_alu_fun), .valE_1(valE_1), .valE_0(valE_0));
  // Probe on aluA_1
  // Probe on aluA_0
  // Probe on valE_1
  // Probe on valE_0
  Cond cond_1 (.CC(register_1_q), .ifun(ifun), .Cnd(Cnd));
  Register #(.width(3)) register_1 (
    .D(alu_1_out_8), .en(main_5_need_cc), .Q(register_1_q), .clk(not_1_out), .clr(Reset));
  // Probe on Cnd
  Prep_Mem prep_mem_1 (
    .valE_1(valE_1), .valE_0(valE_0), .valA_1(valA_1), .valA_0(valA_0), .valP_1({32{1'b0}}), .valP_0(valP),
    .icode(icode), .addr_1(Addr_1), .addr_0(Addr_0), .data_1(Data_1), .data_0(Data_0), .R(prep_mem_1_r),
    .W(prep_mem_1_w));
  // Probe on aluB_1
  // Probe on aluB_0
  // Probe on Addr_1
  // Probe on Addr_0
  // Probe on Data_1
  // Probe on Data_0
  dmem dmem_1 (
    .Addr_1(Addr_1), .Addr_0(Addr_0), .Data_1(Data_1), .Data_0(Data_0), .read(prep_mem_1_r),
    .write(prep_mem_1_w), .valM_1(valM_1), .valM_0(valM_0), .dmemerr(dmemerr), .clock(not_1_out),
    .dataclear(Reset));
  // Probe on valM_1
  // Probe on valM_0
  NewPC newpc_1 (.valC_0(valC_0), .valP_0(valP), .valM_0(valM_0), .cnd(Cnd), .icode(icode), .val(N_PC_output));
  // Probe on NewPC
  Register #(.width(32)) PChold (.D(N_PC_output), .Q(NewPC), .clk(not_1_out), .clr(Reset));  // open: en

  // Notes on the sheet:
  //   Fetch
  //   Decode
  //   Execute
  //   Memory
  //   PC Update
endmodule

module Align (
  input  [7:0] B1,
  input  [7:0] B2,
  input  [7:0] B3,
  input  [7:0] B4,
  input  [7:0] B5,
  input  [7:0] B6,
  input  [7:0] B7,
  input  [7:0] B8,
  input  [7:0] B9,
  input  NeedRegs,
  output [3:0] rA,
  output [3:0] rB,
  output [31:0] valC_1,
  output [31:0] valC_0
);

  // Probe on B1[3:0]
  // Probe on B1[7:4]
  Multiplexer #(.width(4)) multiplexer_1 (.in0(4'b1111), .in1(B1[7:4]), .out(rA), .sel(NeedRegs));  // open: en
  Multiplexer #(.width(4)) multiplexer_2 (.in0(4'b1111), .in1(B1[3:0]), .out(rB), .sel(NeedRegs));  // open: en
  Multiplexer #(.width(32)) multiplexer_3 (
    .in0({B8, B7, B6, B5}), .in1({B9, B8, B7, B6}), .out(valC_1), .sel(NeedRegs));  // open: en
  Multiplexer #(.width(32)) multiplexer_4 (
    .in0({B4, B3, B2, B1}), .in1({B5, B4, B3, B2}), .out(valC_0), .sel(NeedRegs));  // open: en

  // Notes on the sheet:
  //   Goal of align is to come up with the values
endmodule
